// Logisim project TimingQuestion.circ as structural Verilog: 1 circuit, main circuit main
// A
module main (
  input  A,
  input  B,
  input  C,
  output Out
);

  wire and_1_out, and_2_out, and_3_out, clock_1_out, d_ff_1_q, d_ff_2_q, d_ff_3_qn, not_1_out, not_2_out,
       not_3_out, or_1_out, or_2_out, or_3_out, or_4_out, xnor_1_out;

  not not_1 (not_1_out, A);
  not not_2 (not_2_out, B);
  not not_3 (not_3_out, C);
  and and_1 (and_1_out, A, not_2_out);
  and and_2 (and_2_out, d_ff_1_q, C);
  or or_1 (or_1_out, and_1_out, not_3_out);
  and and_3 (and_3_out, not_3_out, not_2_out);
  Clock clock_1 (.out(clock_1_out));
  or or_2 (or_2_out, and_2_out, and_1_out);
  or or_3 (or_3_out, d_ff_2_q, or_1_out);
  or or_4 (or_4_out, or_1_out, and_3_out);
  D_Flip_Flop d_ff_1 (.clk(clock_1_out), .D(or_2_out), .Q(d_ff_1_q));  // open: Qn, preset, en, reset
  D_Flip_Flop d_ff_2 (.clk(clock_1_out), .D(or_3_out), .Q(d_ff_2_q));  // open: Qn, preset, en, reset
  D_Flip_Flop d_ff_3 (.clk(clock_1_out), .D(or_4_out), .Qn(d_ff_3_qn));  // open: Q, preset, en, reset
  xnor xnor_1 (xnor_1_out, d_ff_1_q, d_ff_2_q);
  xnor xnor_2 (Out, xnor_1_out, d_ff_3_qn);

  // Notes on the sheet:
  //   2
  //   4
  //   0
  //   7
  //   9
  //   0
  //   4
  //   7
  //   10
  //   2
  //   10
  //   2
  //   7
  //   2
  //   12
  //   12+3
  //   13+3
  //   13+3
  //   4
  //   4
  //   4
  //   4
  //   10
  //   16
endmodule
