// Logisim project Vending.circ as structural Verilog: 6 circuits, main circuit main
module main (
  input  Halt_Enable
);

  wire and_2_out, CLK, Correct, Dime, Done_Testing, Give_Dime, Give_Merch, Give_Nickel, Halt, Nickel,
       not_1_out, not_2_out, not_3_out, Quarter, Sol_Give_Dime, Sol_Give_Merch, Sol_Give_Nickel;
  wire [8:0] counter_1_q, TestNumber;

  Clock clock_1 (.out(CLK));
  not not_1 (not_1_out, Correct);
  and and_1 (Halt, Halt_Enable, not_1_out);
  Inputs inputs_1 (
    .Halt(Halt), .CLK(CLK), .Quarter(Quarter), .Dime(Dime), .Nickel(Nickel), .TestNumber(TestNumber),
    .Done_Testing(Done_Testing));
  // Probe on Quarter
  // Probe on Dime
  // Probe on Nickel
  Vending vending_1 (
    .Quarter(Quarter), .Dime(Dime), .Nickel(Nickel), .CLK(CLK), .Give_Merchandise(Give_Merch),
    .Give_Dime(Give_Dime), .Give_Nickel(Give_Nickel));
  // Probe on Correct
  // Probe on Give_Merch
  // Probe on Sol_Give_Merch
  // Probe on Give_Dime
  // Probe on Sol_Give_Dime
  // Probe on Give_Nickel
  // Probe on Sol_Give_Nickel
  not not_2 (not_2_out, Halt);
  Checker checker_1 (
    .Give_Merch(Give_Merch), .Give_Dime(Give_Dime), .Give_Nickel(Give_Nickel), .TestNumber(TestNumber),
    .Correct(Correct), .Sol_Give_Merch(Sol_Give_Merch), .Sol_Give_Dime(Sol_Give_Dime),
    .Sol_Give_Nickel(Sol_Give_Nickel));
  and and_2 (and_2_out, Correct, not_2_out, not_3_out);
  not not_3 (not_3_out, Done_Testing);
  Counter #(.width(9), .max('h162), .ongoal("stay")) counter_1 (
    .count(and_2_out), .Q(counter_1_q), .clk(CLK));  // open: load, D, carry, clr
  // Probe on counter_1_q

  // Notes on the sheet:
  //   Max 354
endmodule

module Vending (
  input  Quarter,
  input  Dime,
  input  Nickel,
  input  CLK,
  output Give_Merchandise,
  output Give_Dime,
  output Give_Nickel
);

  wire [2:0] nextstate_1_y0_prime, State;

  NextState nextstate_1 (
    .Y2(State[2]), .Y1(State[1]), .Y0(State[0]), .Quarter(Quarter), .Dime(Dime), .Nickel(Nickel),
    .Y2_Prime(nextstate_1_y0_prime[2]), .Y1_Prime(nextstate_1_y0_prime[1]), .Y0_Prime(nextstate_1_y0_prime[0]));
  Register #(.width(3)) u_State (.D(nextstate_1_y0_prime), .Q(State), .clk(CLK));  // open: en, clr
  Output output_1 (
    .Y2(State[2]), .Y1(State[1]), .Y0(State[0]), .Quarter(Quarter), .Dime(Dime), .Nickel(Nickel),
    .Dispense_Merchandise(Give_Merchandise), .Give_Dime(Give_Dime), .Give_Nickel(Give_Nickel));

  // Other names for the same wires on the sheet: Quater = Quarter
endmodule

module NextState (
  input  Y2,
  input  Y1,
  input  Y0,
  input  Quarter,
  input  Dime,
  input  Nickel,
  output Y2_Prime,
  output Y1_Prime,
  output Y0_Prime
);

  wire and_1_out, and_2_out, and_3_out, and_4_out, and_5_out, and_6_out, and_7_out, and_8_out, and_9_out,
       and_10_out, and_11_out, and_12_out, and_13_out, not_1_out, not_2_out, not_3_out, not_4_out, not_5_out,
       not_6_out, not_7_out, not_8_out, not_9_out, not_10_out, not_11_out, not_12_out, not_13_out,
       not_14_out, not_15_out, not_16_out, not_17_out;

  not not_1 (not_1_out, Y2);
  not not_2 (not_2_out, Y1);
  not not_3 (not_3_out, Y2);
  not not_4 (not_4_out, Quarter);
  not not_5 (not_5_out, Dime);
  not not_6 (not_6_out, Nickel);
  not not_7 (not_7_out, Y2);
  not not_8 (not_8_out, Y2);
  not not_9 (not_9_out, Quarter);
  not not_10 (not_10_out, Dime);
  not not_11 (not_11_out, Nickel);
  not not_12 (not_12_out, Y2);
  not not_13 (not_13_out, Y0);
  not not_14 (not_14_out, Quarter);
  not not_15 (not_15_out, Dime);
  not not_16 (not_16_out, Nickel);
  not not_17 (not_17_out, Y2);
  and and_1 (and_1_out, not_1_out, not_2_out, Quarter);
  and and_2 (and_2_out, Y0, Nickel);
  and and_3 (and_3_out, Y0, Dime);
  and and_4 (and_4_out, not_3_out, Y1, Dime);
  and and_5 (and_5_out, Y2, not_4_out, not_5_out, not_6_out);
  and and_6 (and_6_out, Y2, Y1, Nickel);
  and and_7 (and_7_out, not_7_out, Nickel);
  and and_8 (and_8_out, not_8_out, Dime);
  and and_9 (and_9_out, Y0, Nickel);
  and and_10 (and_10_out, Y1, not_9_out, not_10_out, not_11_out);
  and and_11 (and_11_out, not_12_out, not_13_out, Dime);
  and and_12 (and_12_out, Y0, not_14_out, not_15_out, not_16_out);
  and and_13 (and_13_out, not_17_out, Y1, Nickel);
  or or_1 (Y2_Prime, and_1_out, and_2_out, and_3_out, and_4_out, and_5_out, and_6_out);
  or or_2 (Y1_Prime, and_7_out, and_8_out, and_9_out, and_10_out);
  or or_3 (Y0_Prime, and_11_out, and_12_out, and_13_out);
endmodule

module Output (
  input  Y2,
  input  Y1,
  input  Y0,
  input  Quarter,
  input  Dime,
  input  Nickel,
  output Dispense_Merchandise,
  output Give_Dime,
  output Give_Nickel
);

  wire and_2_out, and_3_out, and_4_out, and_5_out, and_6_out, and_7_out, and_8_out, not_1_out, not_2_out,
       not_3_out, not_4_out, not_5_out;

  not not_1 (not_1_out, Y1);
  not not_2 (not_2_out, Y0);
  and and_1 (Give_Dime, Y2, Quarter);
  not not_3 (not_3_out, Y2);
  not not_4 (not_4_out, Y1);
  not not_5 (not_5_out, Y0);
  and and_2 (and_2_out, Y1, Quarter);
  and and_3 (and_3_out, Y2, not_1_out, Nickel);
  and and_4 (and_4_out, Y2, not_2_out, Dime);
  and and_5 (and_5_out, Y2, Quarter);
  and and_6 (and_6_out, not_3_out, Y0, Quarter);
  and and_7 (and_7_out, Y2, not_4_out, Dime);
  and and_8 (and_8_out, Y2, not_5_out, Quarter);
  or or_1 (Dispense_Merchandise, and_2_out, and_3_out, and_4_out, and_5_out);
  or or_2 (Give_Nickel, and_6_out, and_7_out, and_8_out);
endmodule

module Inputs (
  input  Halt,
  input  CLK,
  output Quarter,
  output Dime,
  output Nickel,
  output [8:0] TestNumber,
  output Done_Testing
);

  wire not_1_out;

  not not_1 (not_1_out, Halt);
  Counter #(.width(9), .max('h162), .ongoal("stay")) counter_1 (
    .count(not_1_out), .Q(TestNumber), .carry(Done_Testing), .clk(CLK));  // open: load, D, clr
  ROM #(.addrWidth(9), .dataWidth(3)) rom_1 (.addr(TestNumber), .data({Quarter, Dime, Nickel}));  // open: sel

  // Notes on the sheet:
  //   contents of rom_1 (hex, n*v repeats v):
  //   1 0 1 0 1 0 1 0 1 0 1 0 1 0 1 0 1 0 1 0 1 0 2 0 1 0 1 0 1 0 1 0 1 0 4 0 1 0 1 0 1 0 1 0 2 0 1 0 1 0
  //   1 0 1 0 4 0 1 0 1 0 1 0 1 0 2 0 1 0 1 0 1 0 2 0 2 0 1 0 1 0 1 0 2 0 4 0 1 0 1 0 1 0 4 0 1 0 1 0 1 0
  //   1 0 2 0 1 0 1 0 1 0 2 0 2 0 1 0 1 0 1 0 2 0 4 0 1 0 1 0 2 0 2 0 1 0 1 0 2 0 4 0 1 0 1 0 4 0 1 0 1 0
  //   1 0 1 0 2 0 1 0 1 0 1 0 2 0 2 0 1 0 1 0 1 0 2 0 4 0 1 0 1 0 2 0 2 0 1 0 1 0 2 0 4 0 1 0 1 0 2 0 2 0
  //   1 0 2 0 2 0 2 0 1 0 2 0 2 0 4 0 1 0 2 0 4 0 1 0 4 0 1 0 1 0 1 0 1 0 2 0 1 0 1 0 1 0 2 0 2 0 1 0 1 0
  //   1 0 2 0 4 0 1 0 1 0 2 0 2 0 1 0 1 0 2 0 4 0 1 0 1 0 2 0 2 0 1 0 2 0 2 0 2 0 1 0 2 0 2 0 4 0 1 0 2 0
  //   4 0 1 0 1 0 2 0 2 0 1 0 2 0 2 0 2 0 1 0 2 0 2 0 4 0 2 0 2 0 2 0 2 0 2 0 4 0 2 0 4 0 1 0 4 0 2 0 4 0
  //   4 0 4
endmodule

module Checker (
  input  Give_Merch,
  input  Give_Dime,
  input  Give_Nickel,
  input  [8:0] TestNumber,
  output Correct,
  output Sol_Give_Merch,
  output Sol_Give_Dime,
  output Sol_Give_Nickel
);

  ROM #(.addrWidth(9), .dataWidth(3)) rom_1 (
    .addr(TestNumber), .data({Sol_Give_Merch, Sol_Give_Dime, Sol_Give_Nickel}));  // open: sel
  Comparator #(.width(3)) comparator_1 (
    .a({Sol_Give_Merch, Sol_Give_Dime, Sol_Give_Nickel}), .b({Give_Merch, Give_Dime, Give_Nickel}),
    .eq(Correct));  // open: gt, lt

  // Other names for the same wires on the sheet: Solution[2:0] = {Sol_Give_Merch, Sol_Give_Dime, Sol_Give_Nickel};
  //   Your_Answer[2:0] = {Give_Merch, Give_Dime, Give_Nickel}

  // Notes on the sheet:
  //   contents of rom_1 (hex, n*v repeats v):
  //   10*0 4 11*0 5 11*0 7 9*0 4 9*0 7 9*0 4 9*0 5 9*0 7 7*0 6 9*0 4 9*0 5 9*0 7 7*0 4 7*0 7 5*0 5 9*0 4
  //   9*0 5 9*0 7 7*0 4 7*0 7 7*0 4 7*0 5 7*0 7 5*0 6 0 0 0 4 9*0 4 9*0 5 9*0 7 7*0 4 7*0 7 7*0 4 7*0 5
  //   7*0 7 5*0 6 7*0 4 7*0 5 7*0 7 5*0 4 5*0 7 0 0 0 5 0 0 0 4 0 0 0 5 0 0 0 7
endmodule
