// Logisim project CPU.circ as structural Verilog: 7 circuits, main circuit CPU
module CPU (
);

  wire CLK, Halt, Is_Immediate, not_1_out, Reg_Write;
  wire [3:0] A, ALU_OP, B_Imm, C, Data_In, multiplexer_1_out, OpCode, Reg_File_a_data, Reg_File_b_data;
  wire [4:0] Program_Counter_q;

  Clock clock_1 (.out(CLK));
  not not_1 (not_1_out, Halt);
  Counter #(.width(5), .max('h1f)) Program_Counter (
    .count(not_1_out), .Q(Program_Counter_q), .clk(CLK));  // open: load, D, carry, clr
  ROM #(.addrWidth(5), .dataWidth(16)) rom_1 (.addr(Program_Counter_q), .data({OpCode, C, A, B_Imm}));  // open: sel
  Decoder Decoder (.OpCode(OpCode), .ALU_OP(ALU_OP), .Reg_Write(Reg_Write), .Is_Immediate(Is_Immediate), .Halt(Halt));
  Reg_File Reg_File (
    .A(A), .B(B_Imm), .C(C), .Data_In(Data_In), .Reg_Write(Reg_Write), .CLK(CLK), .A_DATA(Reg_File_a_data),
    .B_DATA(Reg_File_b_data));
  Multiplexer #(.width(4), .enable("false")) multiplexer_1 (
    .in0(Reg_File_b_data), .in1(B_Imm), .out(multiplexer_1_out), .sel(Is_Immediate));
  ALU ALU (.ALU_OP(ALU_OP), .A(Reg_File_a_data), .B(multiplexer_1_out), .Output(Data_In));

  // Notes on the sheet:
  //   Instructions
  //   contents of rom_1 (hex, n*v repeats v):
  //   2003 2106 1005 3210 4301 5433 6520 763c 8720 986f b938 ca77 db13 ec62 fd85 e05
endmodule

module Decoder (
  input  [3:0] OpCode,
  output [3:0] ALU_OP,
  output Reg_Write,
  output Is_Immediate,
  output Halt
);

  ALU_OP alu_op_1 (
    .Op3(OpCode[3]), .Op2(OpCode[2]), .Op1(OpCode[1]), .Op0(OpCode[0]), .ALU3(ALU_OP[3]), .ALU2(ALU_OP[2]),
    .ALU1(ALU_OP[1]), .ALU0(ALU_OP[0]));
  Reg_Write reg_write_1 (.Op3(OpCode[3]), .Op2(OpCode[2]), .Op1(OpCode[1]), .Op0(OpCode[0]), .Reg_Write(Reg_Write));
  Is_Immediate is_immediate_1 (
    .Op3(OpCode[3]), .Op2(OpCode[2]), .OP1(OpCode[1]), .OP0(OpCode[0]), .Is_Immediate(Is_Immediate));
  Comparator #(.width(4)) comparator_1 (.a(OpCode), .b(4'b0000), .eq(Halt));  // open: gt, lt
endmodule

module ALU (
  input  [3:0] ALU_OP,
  input  [3:0] A,
  input  [3:0] B,
  output [3:0] Output
);

  wire [3:0] ADD_SUB, AND, minus_A, multiplexer_1_out, NOT, not_1_out, OR, XOR;

  assign not_1_out = ~B;  // NOT_Gate not_1, 4 bits wide
  Multiplexer #(.width(4), .enable("false")) multiplexer_1 (
    .in0(B), .in1(not_1_out), .out(multiplexer_1_out), .sel(ALU_OP[3]));
  assign NOT = ~A;  // NOT_Gate not_2, 4 bits wide
  Negator #(.width(4)) negator_1 (.in(A), .out(minus_A));
  Adder #(.width(4)) adder_1 (.a(A), .b(multiplexer_1_out), .out(ADD_SUB), .cin(ALU_OP[3]));  // open: cout
  assign AND = A & B;  // AND_Gate and_1, 4 bits wide
  assign OR = A | B;  // OR_Gate or_1, 4 bits wide
  assign XOR = A ^ B;  // XOR_Gate xor_1, 4 bits wide
  Multiplexer #(.select(3), .width(4), .enable("false")) multiplexer_2 (
    .in0(B), .in1(A), .in2(AND), .in3(OR), .in4(XOR), .in5(NOT), .in6(minus_A), .in7(ADD_SUB), .out(Output),
    .sel(ALU_OP[2:0]));

  // Other names for the same wires on the sheet: DO_SUB = ALU_OP[3]
endmodule

module Reg_File (
  input  [3:0] A,
  input  [3:0] B,
  input  [3:0] C,
  input  [3:0] Data_In,
  input  Reg_Write,
  input  CLK,
  output [3:0] A_DATA,
  output [3:0] B_DATA
);

  wire Write_Reg0, Write_Reg1, Write_Reg2, Write_Reg3, Write_Reg4, Write_Reg5, Write_Reg6, Write_Reg7,
       Write_Reg8, Write_Reg9, Write_Reg10, Write_Reg11, Write_Reg12, Write_Reg13, Write_Reg14, Write_Reg15;
  wire [3:0] Reg0, Reg1, Reg2, Reg3, Reg4, Reg5, Reg6, Reg7, Reg8, Reg9, Reg10, Reg11, Reg12, Reg13, Reg14,
       Reg15;

  Demultiplexer #(.select(4), .enable("false")) demultiplexer_1 (
    .out0(Write_Reg0), .out1(Write_Reg1), .out2(Write_Reg2), .out3(Write_Reg3), .out4(Write_Reg4),
    .out5(Write_Reg5), .out6(Write_Reg6), .out7(Write_Reg7), .out8(Write_Reg8), .out9(Write_Reg9),
    .out10(Write_Reg10), .out11(Write_Reg11), .out12(Write_Reg12), .out13(Write_Reg13), .out14(Write_Reg14),
    .out15(Write_Reg15), .in(Reg_Write), .sel(C));
  // Probe on Reg0
  Register #(.width(4)) u_Reg0 (.D(Data_In), .en(Write_Reg0), .Q(Reg0), .clk(CLK));  // open: clr
  // Probe on Reg4
  Register #(.width(4)) u_Reg4 (.D(Data_In), .en(Write_Reg4), .Q(Reg4), .clk(CLK));  // open: clr
  // Probe on Reg8
  Register #(.width(4)) u_Reg8 (.D(Data_In), .en(Write_Reg8), .Q(Reg8), .clk(CLK));  // open: clr
  // Probe on Reg12
  Register #(.width(4)) u_Reg12 (.D(Data_In), .en(Write_Reg12), .Q(Reg12), .clk(CLK));  // open: clr
  // Probe on Reg1
  Register #(.width(4)) u_Reg1 (.D(Data_In), .en(Write_Reg1), .Q(Reg1), .clk(CLK));  // open: clr
  // Probe on Reg5
  Register #(.width(4)) u_Reg5 (.D(Data_In), .en(Write_Reg5), .Q(Reg5), .clk(CLK));  // open: clr
  // Probe on Reg9
  Register #(.width(4)) u_Reg9 (.D(Data_In), .en(Write_Reg9), .Q(Reg9), .clk(CLK));  // open: clr
  // Probe on Reg13
  Register #(.width(4)) u_Reg13 (.D(Data_In), .en(Write_Reg13), .Q(Reg13), .clk(CLK));  // open: clr
  Register #(.width(4)) u_Reg2 (.D(Data_In), .en(Write_Reg2), .Q(Reg2), .clk(CLK));  // open: clr
  Register #(.width(4)) u_Reg6 (.D(Data_In), .en(Write_Reg6), .Q(Reg6), .clk(CLK));  // open: clr
  Register #(.width(4)) u_Reg10 (.D(Data_In), .en(Write_Reg10), .Q(Reg10), .clk(CLK));  // open: clr
  Register #(.width(4)) u_Reg14 (.D(Data_In), .en(Write_Reg14), .Q(Reg14), .clk(CLK));  // open: clr
  // Probe on Reg2
  // Probe on Reg6
  // Probe on Reg10
  // Probe on Reg14
  // Probe on Reg3
  Register #(.width(4)) u_Reg3 (.D(Data_In), .en(Write_Reg3), .Q(Reg3), .clk(CLK));  // open: clr
  // Probe on Reg7
  Register #(.width(4)) u_Reg7 (.D(Data_In), .en(Write_Reg7), .Q(Reg7), .clk(CLK));  // open: clr
  // Probe on Reg11
  Register #(.width(4)) u_Reg11 (.D(Data_In), .en(Write_Reg11), .Q(Reg11), .clk(CLK));  // open: clr
  // Probe on Reg15
  Register #(.width(4)) u_Reg15 (.D(Data_In), .en(Write_Reg15), .Q(Reg15), .clk(CLK));  // open: clr
  Multiplexer #(.select(4), .width(4), .enable("false")) multiplexer_1 (
    .in0(Reg0), .in1(Reg1), .in2(Reg2), .in3(Reg3), .in4(Reg4), .in5(Reg5), .in6(Reg6), .in7(Reg7),
    .in8(Reg8), .in9(Reg9), .in10(Reg10), .in11(Reg11), .in12(Reg12), .in13(Reg13), .in14(Reg14),
    .in15(Reg15), .out(A_DATA), .sel(A));
  Multiplexer #(.select(4), .width(4), .enable("false")) multiplexer_2 (
    .in0(Reg0), .in1(Reg1), .in2(Reg2), .in3(Reg3), .in4(Reg4), .in5(Reg5), .in6(Reg6), .in7(Reg7),
    .in8(Reg8), .in9(Reg9), .in10(Reg10), .in11(Reg11), .in12(Reg12), .in13(Reg13), .in14(Reg14),
    .in15(Reg15), .out(B_DATA), .sel(B));
endmodule

module ALU_OP (
  input  Op3,
  input  Op2,
  input  Op1,
  input  Op0,
  output ALU3,
  output ALU2,
  output ALU1,
  output ALU0
);

  wire and_2_out, and_3_out, and_4_out, and_5_out, and_6_out, not_1_out, not_2_out, not_3_out;

  and and_1 (ALU3, Op3, Op2, Op1);
  and and_2 (and_2_out, Op3, Op1, Op0);
  not not_1 (not_1_out, Op3);
  and and_3 (and_3_out, not_1_out, not_2_out, Op0);
  not not_2 (not_2_out, Op2);
  and and_4 (and_4_out, Op2, Op1);
  and and_5 (and_5_out, Op3, Op1, not_3_out);
  not not_3 (not_3_out, Op0);
  and and_6 (and_6_out, Op3, Op2);
  or or_1 (ALU1, Op2, and_2_out);
  or or_2 (ALU0, and_3_out, and_4_out, and_5_out, and_6_out);

  assign ALU2 = Op3;
endmodule

module Is_Immediate (
  input  Op3,
  input  Op2,
  input  OP1,
  input  OP0,
  output Is_Immediate
);

  wire and_1_out, and_2_out, and_3_out, not_1_out, not_2_out, not_3_out, not_4_out;

  not not_1 (not_1_out, Op3);
  and and_1 (and_1_out, not_1_out, not_2_out, not_3_out);
  not not_2 (not_2_out, Op2);
  not not_3 (not_3_out, OP0);
  not not_4 (not_4_out, OP1);
  and and_2 (and_2_out, not_4_out, OP0);
  and and_3 (and_3_out, Op2, OP0);
  or or_1 (Is_Immediate, and_1_out, and_2_out, and_3_out);
endmodule

module Reg_Write (
  input  Op3,
  input  Op2,
  input  Op1,
  input  Op0,
  output Reg_Write
);

  or or_1 (Reg_Write, Op1, Op2, Op3);
endmodule
